# Fritzing sketch team5  Untitled Sketch (saved by Fritzing 0.9.3b)
breadboards: 1

parts:
  元件1 = Arduino Uno (Rev3)
  R1 = Resistor [tolerance=±5% resistance=220 package=THT]
  R2 = Resistor [tolerance=±5% resistance=220 package=THT]
  LED1 = LED - 5mm [color="Red (633nm)" package="5 mm [THT]"]
  LED2 = LED - 5mm [color="Red (633nm)" package="5 mm [THT]"]

nets:
  N1: 元件1.D12/MISO, R2.Pin_1
  N2: 元件1.D13/SCK, R1.Pin_1
  N3: 元件1.GND, LED1.cathode, LED2.cathode
  N4: R1.Pin_0, LED2.anode
  N5: R2.Pin_0, LED1.anode
